# Fritzing sketch glove (saved by Fritzing 0.9.4)
breadboards: 1

parts:
  GY1 = GY-521 (MPU-6050) [form="♀ (female)" package=THT]
  U2 = V_REG_LD1117VXX [package=78xxl]
  U3 = LIPO-600mAh [package=lipo-600]
  U4 = ESP32S-HiLetgo [part_number=ESP32S-HiLetgo]
  R3 = Resistor [tolerance=±5% resistance=36 package="0805 [SMD]"]
  R4 = Resistor [tolerance=±5% resistance=220 package="0805 [SMD]"]
  Q2 = npn-Powertransistor [package="TO220 [THT]"]
  U6 = Vibration Motor- ROB-08449 [package=vibe-motor-10mm]
  U7 = SWITCH-SPST-2 [package=switch-spst-vertical]

nets:
  N1: GY1.pin1, U2.OUT, U4.3.3, R3.Pin_1
  GND: GY1.pin2, U2.GND, U3.-, U4.GND
  N2: GY1.pin3, U4.GPIO22
  N3: GY1.pin4, U4.GPIO21
  N4: U2.IN, U7.O
  N5: U3.+, U7.P
  N6: U4.GPIO13, R4.Pin_1
  N7: R3.Pin_0, U6.-
  N8: R4.Pin_0, Q2.base
  N9: Q2.collector, U6.+

custom parts:
  GY-521 (MPU-6050): Placa GY-521 basada en conjunto de acelerómetro+giroscopios MPU-6050
  V_REG_LD1117VXX: LD1117VXX voltage regulator. We carry the 3.3V version (COM-00526) in TO-220 package.
  LIPO-600mAh: 600mAh Lipo-battery
  ESP32S-HiLetgo: HiLetgo ESP-WROOM-32 ESP32 ESP-32S Development Board 2.4GHz Dual-Mode WiFi + Bluetooth Dual Cores Microcontroller The ESP32 integrated with Antenna switches, RF Balun, power amplifiers, low-noise amplifiers, filters, and management modules, and the entire solution occupies the least area of PCB. 2.4 GHz Wi-Fi plus Bluetooth dual-mode chip, with TSMC Ultra-low power consumption 40nm technology,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
