# Fritzing sketch servo_and_stepper (saved by Fritzing 0.9.4)
breadboards: 1

parts:
  Driver1 = 28BYJ-48 Driver Module [part_number=ULN2003 package=THT]
  SM1 = 28BYJ-48 Stepper Motor [part_number=28BYJ-48]
  SERVO1 = Tower Pro SG90 servo [part_number=101246]
  VCC1 = Battery
  U1 = LIPO-600mAh [package=lipo-600]
  U2 = V_REG_LD1117VXX [package=78xxl]
  U3 = ESP32S-HiLetgo [part_number=ESP32S-HiLetgo]

nets:
  N1: Driver1.IN1, U3.GPIO19
  N2: Driver1.IN2, U3.GPIO18
  N3: Driver1.IN3, U3.GPIO5
  N4: Driver1.IN4, U3.GPIO17
  N5: Driver1.GND, VCC1.-
  N6: Driver1.Vmotor, VCC1.+
  N7: Driver1.blue-pin, SM1.blue-pin
  N8: Driver1.pink-pin, SM1.pink-pin
  N9: Driver1.yellow-pin, SM1.red-pin
  N10: Driver1.orange-pin, SM1.orange-pin
  N11: Driver1.red-pin, SM1.yellow-pin
  N12: SERVO1.Signal, U3.GPIO4
  N13: SERVO1.+5V, U2.OUT, U3.3.3
  GND: SERVO1.GND, U1.-, U2.GND, U3.GND
  N14: U1.+, U2.IN

custom parts:
  28BYJ-48 Driver Module: Generic male header
  28BYJ-48 Stepper Motor: Unipolar Stepper Motor 28BYJ-48 Top coil - pink & orange Bottom coil - blue & yellow Common rail - red Connector pins: blue - pink - yellow - orange - red
  Tower Pro SG90 servo: Original file by John De Cristofaro http://www.adafruit.com/products/1449 Adafruit Feedback Servo (Small) Edited by: e-radionica.com 28/9/2015
  Battery: Your standard 2x 18650 battery pack (7,4 Volts)
  LIPO-600mAh: 600mAh Lipo-battery
  V_REG_LD1117VXX: LD1117VXX voltage regulator. We carry the 3.3V version (COM-00526) in TO-220 package.
  ESP32S-HiLetgo: HiLetgo ESP-WROOM-32 ESP32 ESP-32S Development Board 2.4GHz Dual-Mode WiFi + Bluetooth Dual Cores Microcontroller The ESP32 integrated with Antenna switches, RF Balun, power amplifiers, low-noise amplifiers, filters, and management modules, and the entire solution occupies the least area of PCB. 2.4 GHz Wi-Fi plus Bluetooth dual-mode chip, with TSMC Ultra-low power consumption 40nm technology,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
