# Fritzing sketch remote (saved by Fritzing 0.9.4)
breadboards: 1

parts:
  SERVO1 = Tower Pro SG90 servo [part_number=101246]
  U1 = LIPO-600mAh [package=lipo-600]
  U2 = V_REG_LD1117VXX [package=78xxl]
  U3 = ESP32S-HiLetgo [part_number=ESP32S-HiLetgo]
  GY1 = GY-521 (MPU-6050) [form="♀ (female)" package=THT]  # not connected

nets:
  N1: SERVO1.Signal, U3.GPIO4
  N2: SERVO1.+5V, U2.OUT, U3.3.3
  GND: SERVO1.GND, U1.-, U2.GND, U3.GND
  N3: U1.+, U2.IN

custom parts:
  Tower Pro SG90 servo: Original file by John De Cristofaro http://www.adafruit.com/products/1449 Adafruit Feedback Servo (Small) Edited by: e-radionica.com 28/9/2015
  LIPO-600mAh: 600mAh Lipo-battery
  V_REG_LD1117VXX: LD1117VXX voltage regulator. We carry the 3.3V version (COM-00526) in TO-220 package.
  ESP32S-HiLetgo: HiLetgo ESP-WROOM-32 ESP32 ESP-32S Development Board 2.4GHz Dual-Mode WiFi + Bluetooth Dual Cores Microcontroller The ESP32 integrated with Antenna switches, RF Balun, power amplifiers, low-noise amplifiers, filters, and management modules, and the entire solution occupies the least area of PCB. 2.4 GHz Wi-Fi plus Bluetooth dual-mode chip, with TSMC Ultra-low power consumption 40nm technology,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
  GY-521 (MPU-6050): Placa GY-521 basada en conjunto de acelerómetro+giroscopios MPU-6050
