# Fritzing sketch gbbo (saved by Fritzing 0.9.4)
breadboards: 1

parts:
  U1 = ESP32-38PinWide [part_number=ESP32-38PinWide]
  L298N1 = L298N DC motor driver
  M1 = Getriebemotor
  M2 = Getriebemotor
  U2 = LIPO-600mAh [package=lipo-600]
  VCC1 = Battery

nets:
  N1: U1.GPIO33, L298N1.IN4
  N2: U1.GPIO25, L298N1.IN3
  N3: U1.GPIO26, L298N1.IN2
  N4: U1.GPIO27, L298N1.IN1
  GND: U1.GND, L298N1.GND, U2.-, VCC1.-
  N5: U1.VIN, L298N1.5V#7, U2.+
  N6: L298N1.OUT1, M1.pin_1
  N7: L298N1.OUT2, M1.pin_2
  N8: L298N1.OUT3, M2.pin_1
  N9: L298N1.OUT4, M2.pin_2
  N10: L298N1.12V, VCC1.+
  N11: L298N1.5V#9, L298N1.ENA
  N12: L298N1.5V#10, L298N1.ENB

custom parts:
  ESP32-38PinWide: Generic 38-Pin ESP32 with wide format (only access to one side of pins on a breadboard) based on Stephen Lilley's HiLetgo ESP-WROOM-32 ESP32 ESP-32S Development Board.
  L298N DC motor driver: 2x DC motor driver with 78M05 positive voltage regulator (7..35 V) L298N: max 46 V, 2 A Set 5 V Enable jumper to enable 5 V regultor (needed for the L298N) and +5 V output at screw terminal or supply external +5 V at screw terminal Set ENA and/or ENB to +5 V to enable motor permanently or supply ENA and/or ENB with PWM signal IN1 and IN2 set rotation directory for motor A (OUT1/OUT2) IN2 and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
  LIPO-600mAh: 600mAh Lipo-battery
  Battery: Your standard 2x 18650 battery pack (7,4 Volts)
